// Logisim project 13-bit-ALU.circ as structural Verilog: 14 circuits, main circuit main
module ALU_main (
  input  [3:0] Control,
  input  [12:0] A,
  input  [12:0] B,
  output [12:0] oo,
  output Zero,
  output Negative,
  output over,
  output Carry
);

  _13_bit_ALU u_13_bit_alu_1 (
    .A(A), .B(B), .Result(oo), .Zero(Zero), .Negative(Negative), .Overflow(over), .Carry(Carry),
    .Control0(Control[0]), .Control1(Control[1]));
endmodule

// 13-bit AND
module _13_bit_and (
  input  [12:0] A,
  input  [12:0] B,
  output [12:0] R
);

  and and_1 (R[0], A[0], B[0]);
  and and_2 (R[1], A[1], B[1]);
  and and_3 (R[2], A[2], B[2]);
  and and_4 (R[3], A[3], B[3]);
  and and_5 (R[4], A[4], B[4]);
  and and_6 (R[5], A[5], B[5]);
  and and_7 (R[6], A[6], B[6]);
  and and_8 (R[7], A[7], B[7]);
  and and_9 (R[8], A[8], B[8]);
  and and_10 (R[9], A[9], B[9]);
  and and_11 (R[10], A[10], B[10]);
  and and_12 (R[11], A[11], B[11]);
  and and_13 (R[12], A[12], B[12]);
endmodule

// 13-bit OR
module _13_bit_OR (
  input  [12:0] A,
  input  [12:0] B,
  output [12:0] R
);

  or or_1 (R[0], A[0], B[0]);
  or or_2 (R[1], A[1], B[1]);
  or or_3 (R[2], A[2], B[2]);
  or or_4 (R[3], A[3], B[3]);
  or or_5 (R[4], A[4], B[4]);
  or or_6 (R[5], A[5], B[5]);
  or or_7 (R[6], A[6], B[6]);
  or or_8 (R[7], A[7], B[7]);
  or or_9 (R[8], A[8], B[8]);
  or or_10 (R[9], A[9], B[9]);
  or or_11 (R[10], A[10], B[10]);
  or or_12 (R[11], A[11], B[11]);
  or or_13 (R[12], A[12], B[12]);
endmodule

module Full_adder (
  input  Carry_in,
  input  A,
  input  B,
  output Result,
  output Carry_out
);

  wire and_1_out, and_2_out, xor_1_out;

  and and_1 (and_1_out, B, A);
  xor xor_1 (xor_1_out, A, B);
  or or_1 (Carry_out, and_1_out, and_2_out);
  and and_2 (and_2_out, xor_1_out, Carry_in);
  xor xor_2 (Result, Carry_in, xor_1_out);
endmodule

module _13_bit_full_adder (
  input  Carry_in,
  input  A0,
  input  B0,
  input  A1,
  input  B1,
  input  A2,
  input  B2,
  input  A3,
  input  B3,
  input  A4,
  input  B4,
  input  A5,
  input  B5,
  input  A6,
  input  B6,
  input  A7,
  input  B7,
  input  A8,
  input  B8,
  input  A9,
  input  B9,
  input  A10,
  input  B10,
  input  A11,
  input  B11,
  input  A12,
  input  B12,
  output Result0,
  output Result1,
  output Result2,
  output Result3,
  output Result4,
  output Result5,
  output Result6,
  output Result7,
  output Result8,
  output Result9,
  output Result10,
  output Result11,
  output Result12,
  output carry
);

  wire full_adder_1_carry_out, full_adder_2_carry_out, full_adder_3_carry_out, full_adder_4_carry_out,
       full_adder_5_carry_out, full_adder_6_carry_out, full_adder_7_carry_out, full_adder_8_carry_out,
       full_adder_9_carry_out, full_adder_10_carry_out, full_adder_11_carry_out, full_adder_12_carry_out,
       full_adder_13_carry_out;

  Full_adder full_adder_1 (.Carry_in(Carry_in), .A(A0), .B(B0), .Result(Result0), .Carry_out(full_adder_1_carry_out));
  Full_adder full_adder_2 (
    .Carry_in(full_adder_1_carry_out), .A(A1), .B(B1), .Result(Result1), .Carry_out(full_adder_2_carry_out));
  Full_adder full_adder_3 (
    .Carry_in(full_adder_2_carry_out), .A(A2), .B(B2), .Result(Result2), .Carry_out(full_adder_3_carry_out));
  Full_adder full_adder_4 (
    .Carry_in(full_adder_3_carry_out), .A(A3), .B(B3), .Result(Result3), .Carry_out(full_adder_4_carry_out));
  Full_adder full_adder_5 (
    .Carry_in(full_adder_4_carry_out), .A(A4), .B(B4), .Result(Result4), .Carry_out(full_adder_5_carry_out));
  Full_adder full_adder_6 (
    .Carry_in(full_adder_5_carry_out), .A(A5), .B(B5), .Result(Result5), .Carry_out(full_adder_6_carry_out));
  Full_adder full_adder_7 (
    .Carry_in(full_adder_6_carry_out), .A(A6), .B(B6), .Result(Result6), .Carry_out(full_adder_7_carry_out));
  Full_adder full_adder_8 (
    .Carry_in(full_adder_7_carry_out), .A(A7), .B(B7), .Result(Result7), .Carry_out(full_adder_8_carry_out));
  Full_adder full_adder_9 (
    .Carry_in(full_adder_8_carry_out), .A(A8), .B(B8), .Result(Result8), .Carry_out(full_adder_9_carry_out));
  Full_adder full_adder_10 (
    .Carry_in(full_adder_9_carry_out), .A(A9), .B(B9), .Result(Result9), .Carry_out(full_adder_10_carry_out));
  Full_adder full_adder_11 (
    .Carry_in(full_adder_10_carry_out), .A(A10), .B(B10), .Result(Result10),
    .Carry_out(full_adder_11_carry_out));
  Full_adder full_adder_12 (
    .Carry_in(full_adder_11_carry_out), .A(A11), .B(B11), .Result(Result11),
    .Carry_out(full_adder_12_carry_out));
  Full_adder full_adder_13 (
    .Carry_in(full_adder_12_carry_out), .A(A12), .B(B12), .Result(Result12),
    .Carry_out(full_adder_13_carry_out));
endmodule

// FA
module _13_bit_full_adder_concise (
  input  Carry_in,
  input  [12:0] A,
  input  [12:0] B,
  output Carry,
  output [12:0] Result
);

  wire full_adder_1_carry_out, full_adder_2_carry_out, full_adder_3_carry_out, full_adder_4_carry_out,
       full_adder_5_carry_out, full_adder_6_carry_out, full_adder_7_carry_out, full_adder_8_carry_out,
       full_adder_9_carry_out, full_adder_10_carry_out, full_adder_11_carry_out, full_adder_12_carry_out;

  Full_adder full_adder_1 (
    .Carry_in(Carry_in), .A(A[0]), .B(B[0]), .Result(Result[0]), .Carry_out(full_adder_1_carry_out));
  Full_adder full_adder_2 (
    .Carry_in(full_adder_1_carry_out), .A(A[1]), .B(B[1]), .Result(Result[1]),
    .Carry_out(full_adder_2_carry_out));
  Full_adder full_adder_3 (
    .Carry_in(full_adder_2_carry_out), .A(A[2]), .B(B[2]), .Result(Result[2]),
    .Carry_out(full_adder_3_carry_out));
  Full_adder full_adder_4 (
    .Carry_in(full_adder_3_carry_out), .A(A[3]), .B(B[3]), .Result(Result[3]),
    .Carry_out(full_adder_4_carry_out));
  Full_adder full_adder_5 (
    .Carry_in(full_adder_4_carry_out), .A(A[4]), .B(B[4]), .Result(Result[4]),
    .Carry_out(full_adder_5_carry_out));
  Full_adder full_adder_6 (
    .Carry_in(full_adder_5_carry_out), .A(A[5]), .B(B[5]), .Result(Result[5]),
    .Carry_out(full_adder_6_carry_out));
  Full_adder full_adder_7 (
    .Carry_in(full_adder_6_carry_out), .A(A[6]), .B(B[6]), .Result(Result[6]),
    .Carry_out(full_adder_7_carry_out));
  Full_adder full_adder_8 (
    .Carry_in(full_adder_7_carry_out), .A(A[7]), .B(B[7]), .Result(Result[7]),
    .Carry_out(full_adder_8_carry_out));
  Full_adder full_adder_9 (
    .Carry_in(full_adder_8_carry_out), .A(A[8]), .B(B[8]), .Result(Result[8]),
    .Carry_out(full_adder_9_carry_out));
  Full_adder full_adder_10 (
    .Carry_in(full_adder_9_carry_out), .A(A[9]), .B(B[9]), .Result(Result[9]),
    .Carry_out(full_adder_10_carry_out));
  Full_adder full_adder_11 (
    .Carry_in(full_adder_10_carry_out), .A(A[10]), .B(B[10]), .Result(Result[10]),
    .Carry_out(full_adder_11_carry_out));
  Full_adder full_adder_12 (
    .Carry_in(full_adder_11_carry_out), .A(A[11]), .B(B[11]), .Result(Result[11]),
    .Carry_out(full_adder_12_carry_out));
  Full_adder full_adder_13 (
    .Carry_in(full_adder_12_carry_out), .A(A[12]), .B(B[12]), .Result(Result[12]), .Carry_out(Carry));
endmodule

module _13_bit_xor (
  input  Control,
  input  [12:0] B,
  output [12:0] Result
);

  wire [12:0] bit_extender_1_out;

  assign bit_extender_1_out = {{12{Control}}, Control};  // Bit_Extender bit_extender_1
  assign Result = bit_extender_1_out ^ B;  // XOR_Gate xor_1, 13 bits wide
endmodule

// 13-bit \nADD/SUB
module Add_sub (
  input  Sub,
  input  [12:0] A,
  input  [12:0] B,
  output [12:0] Result,
  output Carry,
  output Overflow
);

  wire and_1_out, and_2_out, n12th_bit_out_1__12th_bit, n12th_bit_out_2__12th_bit, n12th_bit_out_3__12th_bit,
       not_1_out, not_2_out, not_3_out;
  wire [12:0] n13_bit_xor_1_result;

  _12th_bit_out u_12th_bit_out_1 (.Input(A), ._12th_bit(n12th_bit_out_1__12th_bit));
  not not_1 (not_1_out, n12th_bit_out_1__12th_bit);
  _12th_bit_out u_12th_bit_out_2 (.Input(B), ._12th_bit(n12th_bit_out_2__12th_bit));
  not not_2 (not_2_out, n12th_bit_out_2__12th_bit);
  _13_bit_xor u_13_bit_xor_1 (.B(B), .Result(n13_bit_xor_1_result), .Control(Sub));
  _13_bit_full_adder_concise u_13_bit_full_adder_concise_1 (
    .Carry_in(Sub), .A(A), .Result(Result), .B(n13_bit_xor_1_result), .Carry(Carry));
  _12th_bit_out u_12th_bit_out_3 (.Input(Result), ._12th_bit(n12th_bit_out_3__12th_bit));
  not not_3 (not_3_out, n12th_bit_out_3__12th_bit);
  and and_1 (and_1_out, not_3_out, n12th_bit_out_2__12th_bit, n12th_bit_out_1__12th_bit);
  and and_2 (and_2_out, n12th_bit_out_3__12th_bit, not_2_out, not_1_out);
  or or_1 (Overflow, and_1_out, and_2_out);

  // Notes on the sheet:
  //   A31
  //   B31
  //   Result 12
endmodule

// 12th
module _12th_bit_out (
  input  [12:0] Input,
  output _12th_bit
);


  assign _12th_bit = Input[12];
endmodule

// Reduce-OR
module _13_bit_reduce_or (
  input  [12:0] Input,
  output Output
);

  or or_1 (Output, Input[0], Input[1], Input[2], Input[3], Input[4], Input[5], Input[6], Input[7], Input[8], Input[9], Input[10], Input[11], Input[12]);
endmodule

module _13_bit_ALU (
  input  Control0,
  input  Control1,
  input  [12:0] A,
  input  [12:0] B,
  output [12:0] Result,
  output Zero,
  output Negative,
  output Overflow,
  output Carry
);

  wire n13_bit_reduce_or_1_output;
  wire [12:0] add_sub_1_result, multiplexer_1_out, n13_bit_and_1_r, n13_bit_or_1_r;

  _13_bit_and u_13_bit_and_1 (.A(A), .B(B), .R(n13_bit_and_1_r));
  _13_bit_OR u_13_bit_or_1 (.A(A), .R(n13_bit_or_1_r), .B(B));
  Add_sub add_sub_1 (.Sub(Control0), .A(A), .B(B), .Result(add_sub_1_result), .Carry(Carry), .Overflow(Overflow));
  Multiplexer #(.width(13), .enable("false")) multiplexer_1 (
    .in0(n13_bit_and_1_r), .in1(n13_bit_or_1_r), .out(multiplexer_1_out), .sel(Control0));
  Multiplexer #(.width(13), .enable("false")) multiplexer_2 (
    .in0(multiplexer_1_out), .in1(add_sub_1_result), .out(Result), .sel(Control1));
  _12th_bit_out u_12th_bit_out_1 (.Input(Result), ._12th_bit(Negative));
  _13_bit_reduce_or u_13_bit_reduce_or_1 (.Input(Result), .Output(n13_bit_reduce_or_1_output));
  not not_1 (Zero, n13_bit_reduce_or_1_output);
endmodule

module booth_s_multiplier (
  input  [12:0] M_input,
  input  [12:0] Q_input,
  input  Reset,
  input  Enable,
  input  clk1,
  output [12:0] exp,
  output [25:0] result
);

  wire A_out, and_1_out, cu_mul_1_c0, cu_mul_1_c1, cu_mul_1_cl__a__q_1, cu_mul_1_dec_cnt,
       cu_mul_1_load__m__q__cnt, cu_mul_1_load_a, cu_mul_1_shr, or_1_out, Q__1_q0, Q_out;
  wire [3:0] counter_1_q;
  wire [12:0] M_q12, n13_bit_alu_1_result, register_1_q, register_2_q;

  Register #(.width(13)) register_1 (.D(Q_input), .Q(register_1_q), .clk(and_1_out), .clr(Reset));  // open: en
  cu_mul cu_mul_1 (
    .Clk(and_1_out), .Reset(Reset), .Q0(exp[0]), .Q_1(Q__1_q0), .Count(counter_1_q),
    .Cl__A__Q_1(cu_mul_1_cl__a__q_1), .LOad__M__Q__Cnt(cu_mul_1_load__m__q__cnt), .Load_A(cu_mul_1_load_a),
    .C0(cu_mul_1_c0), .C1(cu_mul_1_c1), .Shr(cu_mul_1_shr), .Dec_Cnt(cu_mul_1_dec_cnt));
  and and_1 (and_1_out, Enable, clk1);
  Register #(.width(13)) register_2 (.D(M_input), .Q(register_2_q), .clk(and_1_out), .clr(Reset));  // open: en
  or or_1 (or_1_out, cu_mul_1_load__m__q__cnt, cu_mul_1_dec_cnt);
  Counter #(.width(4), .max('hd)) counter_1 (
    .load(or_1_out), .D(4'b1101), .count(cu_mul_1_dec_cnt), .Q(counter_1_q), .clk(and_1_out));  // open: carry, clr
  Counter counter_2 (.clk(and_1_out), .clr(Reset));  // open: load, D, count, Q, carry
  Shift_Register #(.length(13)) A (
    .shift(cu_mul_1_shr), .in(result[25]), .clk(and_1_out), .out(A_out), .load(cu_mul_1_load_a), .clr(Reset),
    .d0(n13_bit_alu_1_result[12]), .q0(result[25]), .d1(n13_bit_alu_1_result[11]), .q1(result[24]),
    .d2(n13_bit_alu_1_result[10]), .q2(result[23]), .d3(n13_bit_alu_1_result[9]), .q3(result[22]),
    .d4(n13_bit_alu_1_result[8]), .q4(result[21]), .d5(n13_bit_alu_1_result[7]), .q5(result[20]),
    .d6(n13_bit_alu_1_result[6]), .q6(result[19]), .d7(n13_bit_alu_1_result[5]), .q7(result[18]),
    .d8(n13_bit_alu_1_result[4]), .q8(result[17]), .d9(n13_bit_alu_1_result[3]), .q9(result[16]),
    .d10(n13_bit_alu_1_result[2]), .q10(result[15]), .d11(n13_bit_alu_1_result[1]), .q11(result[14]),
    .d12(n13_bit_alu_1_result[0]), .q12(result[13]));
  Shift_Register #(.length(13)) M (
    .shift(1'b0), .clk(and_1_out), .load(cu_mul_1_load__m__q__cnt), .clr(Reset), .d0(register_2_q[12]),
    .q0(M_q12[12]), .d1(register_2_q[11]), .q1(M_q12[11]), .d2(register_2_q[10]), .q2(M_q12[10]),
    .d3(register_2_q[9]), .q3(M_q12[9]), .d4(register_2_q[8]), .q4(M_q12[8]), .d5(register_2_q[7]),
    .q5(M_q12[7]), .d6(register_2_q[6]), .q6(M_q12[6]), .d7(register_2_q[5]), .q7(M_q12[5]),
    .d8(register_2_q[4]), .q8(M_q12[4]), .d9(register_2_q[3]), .q9(M_q12[3]), .d10(register_2_q[2]),
    .q10(M_q12[2]), .d11(register_2_q[1]), .q11(M_q12[1]), .d12(register_2_q[0]), .q12(M_q12[0]));  // open: in, out
  Shift_Register #(.length(13)) Q (
    .shift(cu_mul_1_shr), .in(A_out), .clk(and_1_out), .out(Q_out), .load(cu_mul_1_load__m__q__cnt),
    .clr(Reset), .d0(register_1_q[12]), .q0(exp[12]), .d1(register_1_q[11]), .q1(exp[11]),
    .d2(register_1_q[10]), .q2(exp[10]), .d3(register_1_q[9]), .q3(exp[9]), .d4(register_1_q[8]),
    .q4(exp[8]), .d5(register_1_q[7]), .q5(exp[7]), .d6(register_1_q[6]), .q6(exp[6]), .d7(register_1_q[5]),
    .q7(exp[5]), .d8(register_1_q[4]), .q8(exp[4]), .d9(register_1_q[3]), .q9(exp[3]), .d10(register_1_q[2]),
    .q10(exp[2]), .d11(register_1_q[1]), .q11(exp[1]), .d12(register_1_q[0]), .q12(exp[0]));
  Shift_Register #(.length(1)) Q__1 (
    .shift(cu_mul_1_shr), .in(Q_out), .clk(and_1_out), .clr(cu_mul_1_cl__a__q_1), .q0(Q__1_q0));  // open: out, load, d0
  _13_bit_ALU u_13_bit_alu_1 (
    .A(result[25:13]), .B(M_q12), .Result(n13_bit_alu_1_result), .Control0(cu_mul_1_c0),
    .Control1(cu_mul_1_c1));  // open: Zero, Negative, Overflow, Carry

  assign result[12:0] = exp;
endmodule

module cu_mul (
  input  Clk,
  input  Reset,
  input  Q0,
  input  Q_1,
  input  [3:0] Count,
  output Cl__A__Q_1,
  output LOad__M__Q__Cnt,
  output Load_A,
  output C0,
  output C1,
  output Shr,
  output Dec_Cnt
);

  wire and_3_out, multiplexer_1_out, not_1_out, not_2_out, not_3_out, not_4_out, not_5_out, not_6_out,
       not_7_out, or_2_out, Q0_prime_Q_1_out, Q0Q_1_prime_out;
  wire [1:0] rom_1_data_2;
  wire [2:0] and_1_out, and_2_out, bit_extender_1_out, bit_extender_2_out, bit_extender_3_out, CAR_q,
       or_1_out, rom_1_data;

  assign bit_extender_1_out = {{2{Q0_prime_Q_1_out}}, Q0_prime_Q_1_out};  // Bit_Extender bit_extender_1
  and Q0_prime_Q_1 (Q0_prime_Q_1_out, not_2_out, Q_1);
  not not_1 (not_1_out, Q0_prime_Q_1_out);
  assign bit_extender_2_out = {{2{not_1_out}}, not_1_out};  // Bit_Extender bit_extender_2
  assign and_1_out = 3'b100 & bit_extender_3_out & bit_extender_1_out;  // AND_Gate and_1, 3 bits wide
  assign or_1_out = and_1_out | rom_1_data | and_2_out;  // OR_Gate or_1, 3 bits wide
  not not_2 (not_2_out, Q0);
  assign and_2_out = bit_extender_2_out & bit_extender_3_out & 3'b101;  // AND_Gate and_2, 3 bits wide
  assign bit_extender_3_out = {{2{and_3_out}}, and_3_out};  // Bit_Extender bit_extender_3
  and and_3 (and_3_out, not_3_out, CAR_q[1], not_4_out);
  not not_3 (not_3_out, CAR_q[2]);
  not not_4 (not_4_out, CAR_q[0]);
  Counter #(.width(3), .max('h7)) CAR (
    .load(not_5_out), .D(or_1_out), .count(multiplexer_1_out), .Q(CAR_q), .clk(Clk), .clr(Reset));  // open: carry
  not not_5 (not_5_out, multiplexer_1_out);
  Multiplexer #(.select(2), .enable("false")) multiplexer_1 (
    .in0(1'b0), .in1(1'b1), .in2(Q0Q_1_prime_out), .in3(not_7_out), .out(multiplexer_1_out),
    .sel(rom_1_data_2));
  ROM #(.addrWidth(3), .dataWidth(12)) rom_1 (
    .addr(CAR_q), .data({Cl__A__Q_1, LOad__M__Q__Cnt, Load_A, C0, C1, Shr, Dec_Cnt, rom_1_data, rom_1_data_2}));  // open: sel
  and Q0Q_1_prime (Q0Q_1_prime_out, not_6_out, Q0);
  not not_6 (not_6_out, Q_1);
  not not_7 (not_7_out, or_2_out);
  or or_2 (or_2_out, Count[0], Count[1], Count[2], Count[3]);

  // Notes on the sheet:
  //   To choose only
  //   state 2 (010)
  //   Control Word Format: Clear (A, Q-1), Load (M, Q, Cnt), Load A, C0, C1, Shr, Dec Cnt, Address bits (3 bit), Selection bits (2 bit)
  //   contents of rom_1 (hex, n*v repeats v):
  //   1 c01 2 394 281 61 b 1c
endmodule

// ctrl_op
module main (
  input  [12:0] a,
  input  [12:0] b,
  input  [3:0] control_signal,
  input  reset,
  output [12:0] and_or_add_sub,
  output [12:0] alu_output,
  output [12:0] inc_dec_2_s_comp,
  output [25:0] mul
);

  wire and_1_out, clock_1_out, not_1_out, not_2_out;
  wire [1:0] rom_3_data;
  wire [2:0] rom_1_data_3;
  wire [3:0] rom_1_data_2, rom_2_data;
  wire [12:0] booth_s_multiplier_1_exp, multiplexer_1_out, undriven, xor_1_out;
  wire [13:4] rom_1_data;

  assign xor_1_out = a ^ {13{1'b1}};  // XOR_Gate xor_1, 13 bits wide
  ROM #(.addrWidth(4), .dataWidth(14)) rom_1 (
    .addr(control_signal), .data({rom_1_data[13:12], rom_1_data_3, rom_1_data[8:4], rom_1_data_2}));  // open: sel
  and and_1 (and_1_out, rom_1_data_3[2], not_1_out, not_2_out);
  Multiplexer #(.width(13), .enable("false")) multiplexer_1 (
    .in0(a), .in1(xor_1_out), .out(multiplexer_1_out), .sel(and_1_out));
  Clock clock_1 (.out(clock_1_out));
  not not_1 (not_1_out, rom_1_data_3[1]);
  not not_2 (not_2_out, rom_1_data_3[0]);
  booth_s_multiplier booth_s_multiplier_1 (
    .M_input(a), .Q_input(b), .Reset(reset), .Enable(rom_1_data[12]), .clk1(clock_1_out),
    .exp(booth_s_multiplier_1_exp), .result(mul));
  ALU_main alu_main_1 (.Control(rom_1_data_2), .A(a), .B(b), .oo(and_or_add_sub));  // open: Zero, Negative, over, Carry
  ROM #(.addrWidth(3), .dataWidth(4)) rom_2 (.addr(rom_1_data_3), .data(rom_2_data));  // open: sel
  ALU_main alu_main_2 (
    .Control(rom_2_data), .A(multiplexer_1_out), .B(13'h1), .oo(inc_dec_2_s_comp));  // open: Zero, Negative, over, Carry
  Multiplexer #(.select(2), .width(13), .enable("false")) multiplexer_2 (
    .in0(and_or_add_sub), .in1(inc_dec_2_s_comp), .in2(booth_s_multiplier_1_exp), .in3(undriven),
    .out(alu_output), .sel(rom_3_data));
  ROM #(.addrWidth(4), .dataWidth(2)) rom_3 (.addr(control_signal), .data(rom_3_data));  // open: sel

  // Notes on the sheet:
  //   contents of rom_1 (hex, n*v repeats v):
  //   0 1 2 3 4 5*0 200 400 800 1000 2000
  //   contents of rom_2 (hex, n*v repeats v):
  //   0 2 3 0 2
  //   contents of rom_3 (hex, n*v repeats v):
  //   4*0 1 1 1 2 3 0 1 1 1 2 3
endmodule
