// Logisim project 13_bit_cpu.circ as structural Verilog: 3 circuits, main circuit main
module main (
);

  wire clock_1_out, cpu_1_r, cpu_1_w, Reset_out;
  wire [8:0] cpu_1_addr;
  wire [12:0] cpu_1_dataout, ram_1_data;

  Clock clock_1 (.out(clock_1_out));
  Button Reset (.out(Reset_out));
  CPU cpu_1 (
    .Clk(clock_1_out), .Reset(Reset_out), .R(cpu_1_r), .W(cpu_1_w), .Addr(cpu_1_addr), .DataIn(ram_1_data),
    .DataOut(cpu_1_dataout));
  RAM #(.addrWidth(9), .dataWidth(13), .bus("separate")) ram_1 (
    .addr(cpu_1_addr), .din(cpu_1_dataout), .data(ram_1_data), .str(cpu_1_w), .clk(clock_1_out), .ld(cpu_1_r));  // open: sel, clr

  // Notes on the sheet:
  //   0 - AND
  //   1 - OR
  //   2 - ADD
  //   3 - SUB
  //   4 - STO
  //   5 - LDA
  //   6 - BUN
  //   7 - JZ
  //   8 - HLT
  //   9 - JNZ
  //   A - INC
  //   B - DEC
  //   C - 2's Complement
  //   d-mul
endmodule

module CPU (
  input  Clk,
  input  Reset,
  input  [12:0] DataIn,
  output R,
  output W,
  output [8:0] Addr,
  output [12:0] DataOut
);

  wire and_1_out, and_2_out, and_3_out, and_4_out, and_5_out, b1, b3, b4, c0, c1, comparator_1_eq,
       comparator_2_lt, comparator_3_eq, comparator_3_lt, controlunit_1_c1, controlunit_1_loadac,
       controlunit_1_loadsignal, d1, d2, LdA, LdA_from_MBR, LoadAc, LoadB, LoadMAR, multiplexer_6_out,
       nor_1_out, not_1_out, or_5_out;
  wire [3:0] IR_q;
  wire [7:0] counter_2_q;
  wire [8:0] counter_1_q, multiplexer_1_out;
  wire [12:0] _1_s, Ac, Ac_q, AcIn, ALUout, multiplexer_3_out, multiplexer_4_out, multiplexer_5_out;

  Multiplexer #(.width(9), .enable("false")) multiplexer_1 (
    .in0(counter_1_q), .in1(DataOut[8:0]), .out(multiplexer_1_out), .sel(d2));
  Multiplexer #(.width(13), .enable("false")) multiplexer_2 (
    .in0(ALUout), .in1(DataOut), .out(AcIn), .sel(LdA_from_MBR));
  and and_1 (and_1_out, or_5_out, Clk);
  Comparator #(.width(4)) comparator_1 (.a(IR_q), .b(4'b1101), .eq(comparator_1_eq));  // open: gt, lt
  Counter #(.width(9), .max('h1ff)) counter_1 (
    .load(controlunit_1_loadsignal), .D(DataOut[8:0]), .count(controlunit_1_c1), .Q(counter_1_q),
    .clk(and_1_out), .clr(Reset));  // open: carry
  Register #(.width(9)) MAR (.D(multiplexer_1_out), .en(LoadMAR), .Q(Addr), .clk(and_1_out), .clr(Reset));
  Register #(.width(4)) IR (.D(DataOut[12:9]), .en(controlunit_1_c1), .Q(IR_q), .clk(and_1_out), .clr(Reset));
  ControlUnit controlunit_1 (
    .IR(DataOut[12:9]), .Reset(Reset), .Clk(and_1_out), .d1(d1), .c1(controlunit_1_c1), .R(R), .d2(d2),
    .Operation({c0, c1}), .b1(b1), .W(W), .LoadAc(controlunit_1_loadac), .b3(b3), .LdAfrB(LdA_from_MBR),
    .ZF_in(nor_1_out), .LoadSignal(controlunit_1_loadsignal), .b4(b4));  // open: c2, b2
  and and_2 (and_2_out, Clk, comparator_1_eq);
  not not_1 (not_1_out, comparator_1_eq);
  Counter #(.max('h2e)) counter_2 (.Q(counter_2_q), .clk(and_2_out));  // open: load, D, count, carry, clr
  Multiplexer #(.width(13)) multiplexer_3 (
    .in0(multiplexer_4_out), .in1(13'h1), .out(multiplexer_3_out), .sel(b3));  // open: en
  Multiplexer #(.width(13), .enable("false")) multiplexer_4 (.in0(DataIn), .in1(Ac), .out(multiplexer_4_out), .sel(b1));
  Multiplexer #(.width(13)) multiplexer_5 (.in0(AcIn), .in1(Ac), .out(multiplexer_5_out), .sel(b4));  // open: en
  or or_1 (LdA, controlunit_1_loadac, comparator_3_eq);
  or or_2 (LoadMAR, d1, d2);
  Comparator comparator_2 (.a(counter_2_q), .b(8'h4), .lt(comparator_2_lt));  // open: gt, eq
  Comparator comparator_3 (.a(counter_2_q), .b(8'h2e), .eq(comparator_3_eq), .lt(comparator_3_lt));  // open: gt
  Register #(.width(13)) MBR (.D(multiplexer_3_out), .en(LoadB), .Q(DataOut), .clk(and_1_out), .clr(Reset));
  Register #(.width(13)) u_Ac (.D(multiplexer_5_out), .en(LoadAc), .Q(Ac_q), .clk(and_1_out), .clr(Reset));
  and and_3 (and_3_out, comparator_1_eq, comparator_3_eq);
  and and_4 (and_4_out, comparator_2_lt, comparator_1_eq);
  or or_3 (LoadB, R, b3, b1);
  or or_4 (LoadAc, LdA_from_MBR, b4, multiplexer_6_out);
  Multiplexer #(.enable("false")) multiplexer_6 (.in0(LdA), .in1(1'b0), .out(multiplexer_6_out), .sel(and_5_out));
  or or_5 (or_5_out, and_3_out, and_4_out, not_1_out);
  and and_5 (and_5_out, comparator_1_eq, comparator_3_lt);
  not not_2 (_1_s[0], Ac_q[0]);
  not not_3 (_1_s[1], Ac_q[1]);
  not not_4 (_1_s[2], Ac_q[2]);
  not not_5 (_1_s[3], Ac_q[3]);
  not not_6 (_1_s[4], Ac_q[4]);
  not not_7 (_1_s[5], Ac_q[5]);
  not not_8 (_1_s[6], Ac_q[6]);
  not not_9 (_1_s[7], Ac_q[7]);
  not not_10 (_1_s[8], Ac_q[8]);
  not not_11 (_1_s[9], Ac_q[9]);
  not not_12 (_1_s[10], Ac_q[10]);
  not not_13 (_1_s[11], Ac_q[11]);
  not not_14 (_1_s[12], Ac_q[12]);
  _13_bit_ALU_main main_1 (
    .a(Ac), .b(DataOut), .control_signal(IR_q), .reset(and_4_out), .alu_output(ALUout));  // open: and_or_add_sub, inc_dec_2_s_comp, mul
  Multiplexer #(.width(13)) multiplexer_7 (.in0(Ac_q), .in1(_1_s), .out(Ac), .sel(b4));  // open: en
  nor nor_1 (nor_1_out, Ac[0], Ac[1], Ac[2], Ac[3], Ac[4], Ac[5], Ac[6], Ac[7], Ac[8], Ac[9], Ac[10], Ac[11], Ac[12]);

  // Other names for the same wires on the sheet: clr = Reset; MBRout[12:0] = DataOut
endmodule

// CU
module ControlUnit (
  input  [3:0] IR,
  input  Clk,
  input  Reset,
  input  ZF_in,
  output d1,
  output c1,
  output R,
  output c2,
  output d2,
  output [1:0] Operation,
  output b1,
  output W,
  output b2,
  output LoadAc,
  output b3,
  output LdAfrB,
  output LoadSignal,
  output b4
);

  wire and_1_out, and_2_out, and_3_out, decoder_1_out6, decoder_1_out7, decoder_1_out8, decoder_1_out9,
       decoder_1_out15, not_1_out, not_2_out, or_1_out;
  wire [5:0] counter_1_q;
  wire [7:0] rom_1_data;

  Counter #(.width(6), .max('h3f)) counter_1 (
    .load(rom_1_data[2]), .D({IR, 2'b11}), .count(rom_1_data[0]), .Q(counter_1_q), .clk(and_1_out),
    .clr(or_1_out));  // open: carry
  or or_1 (or_1_out, rom_1_data[1], Reset);
  and and_1 (and_1_out, Clk, not_1_out);
  ROM #(.addrWidth(6)) rom_1 (.addr(counter_1_q), .data(rom_1_data));  // open: sel
  Decoder #(.select(5)) decoder_1 (
    .out1(d1), .out2(c1), .out3(R), .out4(c2), .out5(d2), .out6(decoder_1_out6), .out7(decoder_1_out7),
    .out8(decoder_1_out8), .out9(decoder_1_out9), .out10(b1), .out11(W), .out12(b2), .out13(b3),
    .out14(LdAfrB), .out15(decoder_1_out15), .out16(b4), .sel(rom_1_data[7:3]));  // open: out0, out17, out18, out19, out20, out21, out22, out23, out24, out25, out26, out27, out28, out29, out30, out31, en
  not not_1 (not_1_out, decoder_1_out15);
  Priority_Encoder #(.select(2)) priority_encoder_1 (
    .in0(decoder_1_out6), .in1(decoder_1_out7), .in2(decoder_1_out8), .in3(decoder_1_out9), .out(Operation));  // open: gs, en_out, en_in
  and and_2 (and_2_out, c2, ZF_in);
  not not_2 (not_2_out, ZF_in);
  or or_2 (LoadAc, decoder_1_out6, decoder_1_out7, decoder_1_out8, decoder_1_out9);
  and and_3 (and_3_out, not_2_out, b2);
  or or_3 (LoadSignal, and_2_out, and_3_out);

  // Notes on the sheet:
  //   contents of rom_1 (hex, n*v repeats v):
  //   9 19 14 29 19 31 2 29 19 41 2 29 19 39 2 29 19 49 2 29 51 59 2 29 19 71 2 21 2 2 2 21 2 0 0 7a 0 0 0
  //   61 2 0 0 69 39 2 0 69 49 2 0 81 19 a9 2 29 19 41 2 b9
endmodule
